# Fritzing sketch I2C probeersel (saved by Fritzing 0.9.3b)

parts:
  Onderdeel4 = Arduino Uno (Rev3)
  Matrix_keypad3 = KEYPAD 4x4
  Onderdeel5 = RFID USB Reader
  Onderdeel6 = Arduino Uno (Rev3)
  Matrix_keypad4 = KEYPAD 4x4
  Onderdeel7 = RFID USB Reader
  Onderdeel8 = Arduino Uno (Rev3)
  Matrix_keypad5 = KEYPAD 4x4
  Onderdeel9 = RFID USB Reader
  Onderdeel10 = Arduino Uno (Rev3)
  Matrix_keypad6 = KEYPAD 4x4
  Onderdeel11 = RFID USB Reader
  Onderdeel12 = Arduino Due (Rev2b)
  Onderdeel14 = Thermal Printer

nets:
  N1: Onderdeel4.A2, Matrix_keypad3.row4
  N2: Onderdeel4.A3, Matrix_keypad3.row3
  N3: Onderdeel4.D9_PWM, Onderdeel5.GND
  N4: Onderdeel4.D10_PWM/SS, Onderdeel5.GNDT
  N5: Onderdeel4.D11_PWM/MOSI, Onderdeel5.ANT2
  N6: Onderdeel4.D12/MISO, Onderdeel5.ANT1
  N7: Onderdeel4.D13/SCK, Onderdeel5.CP
  N8: Onderdeel4.D2, Matrix_keypad3.row2
  N9: Onderdeel4.D3_PWM, Matrix_keypad3.row1
  N10: Onderdeel4.D4, Matrix_keypad3.col4
  N11: Onderdeel4.D5_PWM, Matrix_keypad3.col3
  N12: Onderdeel4.D6_PWM, Matrix_keypad3.col2
  N13: Onderdeel4.D7, Matrix_keypad3.col1
  3V3: Onderdeel4.3V3, Onderdeel5.VCC
  GND: Onderdeel4.GND, Onderdeel5.TX-O-RS232, Onderdeel5.TX-O, Onderdeel8.GND, Onderdeel9.TX-O-RS232, Onderdeel9.TX-O, Onderdeel14.GND#2
  VIN: Onderdeel4.VIN, Onderdeel8.VIN, Onderdeel14.VH
  N14: Onderdeel6.A2, Matrix_keypad4.row4
  N15: Onderdeel6.A3, Matrix_keypad4.row3
  N16: Onderdeel6.D9_PWM, Onderdeel7.GND
  N17: Onderdeel6.D10_PWM/SS, Onderdeel7.GNDT
  N18: Onderdeel6.D11_PWM/MOSI, Onderdeel7.ANT2
  N19: Onderdeel6.D12/MISO, Onderdeel7.ANT1
  N20: Onderdeel6.D13/SCK, Onderdeel7.CP
  N21: Onderdeel6.D2, Matrix_keypad4.row2
  N22: Onderdeel6.D3_PWM, Matrix_keypad4.row1
  N23: Onderdeel6.D4, Matrix_keypad4.col4
  N24: Onderdeel6.D5_PWM, Matrix_keypad4.col3
  N25: Onderdeel6.D6_PWM, Matrix_keypad4.col2
  N26: Onderdeel6.D7, Matrix_keypad4.col1
  3V3_2: Onderdeel6.3V3, Onderdeel7.VCC
  N27: Onderdeel6.GND, Onderdeel7.TX-O-RS232, Onderdeel7.TX-O
  N28: Onderdeel8.A2, Matrix_keypad5.row4
  N29: Onderdeel8.A3, Matrix_keypad5.row3
  N30: Onderdeel8.A4/SDA, Onderdeel12.D21/SCL3
  N31: Onderdeel8.A5/SCL, Onderdeel12.D20/SDA3
  N32: Onderdeel8.D9_PWM, Onderdeel9.GND
  N33: Onderdeel8.D10_PWM/SS, Onderdeel9.GNDT
  N34: Onderdeel8.D11_PWM/MOSI, Onderdeel9.ANT2
  N35: Onderdeel8.D12/MISO, Onderdeel9.ANT1
  N36: Onderdeel8.D13/SCK, Onderdeel9.CP
  N37: Onderdeel8.D2, Matrix_keypad5.row2
  N38: Onderdeel8.D3_PWM, Matrix_keypad5.row1
  N39: Onderdeel8.D4, Matrix_keypad5.col4
  N40: Onderdeel8.D5_PWM, Matrix_keypad5.col3
  N41: Onderdeel8.D6_PWM, Matrix_keypad5.col2
  N42: Onderdeel8.D7, Matrix_keypad5.col1
  3V3_3: Onderdeel8.3V3, Onderdeel9.VCC
  N43: Onderdeel10.A2, Matrix_keypad6.row4
  N44: Onderdeel10.A3, Matrix_keypad6.row3
  N45: Onderdeel10.D9_PWM, Onderdeel11.GND
  N46: Onderdeel10.D10_PWM/SS, Onderdeel11.GNDT
  N47: Onderdeel10.D11_PWM/MOSI, Onderdeel11.ANT2
  N48: Onderdeel10.D12/MISO, Onderdeel11.ANT1
  N49: Onderdeel10.D13/SCK, Onderdeel11.CP
  GND_2: Onderdeel10.GND, Onderdeel11.TX-O-RS232, Onderdeel11.TX-O, Onderdeel12.GND
  N50: Onderdeel10.D2, Matrix_keypad6.row2
  N51: Onderdeel10.D3_PWM, Matrix_keypad6.row1
  N52: Onderdeel10.D4, Matrix_keypad6.col4
  N53: Onderdeel10.D5_PWM, Matrix_keypad6.col3
  N54: Onderdeel10.D6_PWM, Matrix_keypad6.col2
  N55: Onderdeel10.D7, Matrix_keypad6.col1
  3V3_4: Onderdeel10.3V3, Onderdeel11.VCC
  VIN_2: Onderdeel10.VIN, Onderdeel12.5V
  N56: Onderdeel12.D8_PWM, Onderdeel14.RXD
  N57: Onderdeel12.D9_PWM, Onderdeel14.TXD

custom parts:
  KEYPAD 4x4: Matrix keypad 16 buttons, 4 rows x 4 columns
