# Fritzing sketch RFID with Keypad (uno) v1.0 (saved by Fritzing 0.9.3b)

parts:
  Onderdeel2 = RFID USB Reader
  Matrix_keypad2 = KEYPAD 4x4
  Onderdeel3 = Arduino Uno (Rev3)

nets:
  N1: Onderdeel2.GNDT, Onderdeel3.D10_PWM/SS
  N2: Onderdeel2.CP, Onderdeel3.D13/SCK
  N3: Onderdeel2.ANT2, Onderdeel3.D11_PWM/MOSI
  N4: Onderdeel2.ANT1, Onderdeel3.D12/MISO
  N5: Onderdeel2.TX-O-RS232, Onderdeel2.TX-O, Onderdeel3.GND
  N6: Onderdeel2.GND, Onderdeel3.D9_PWM
  VCC: Onderdeel2.VCC, Onderdeel3.3V3
  N7: Matrix_keypad2.col1, Onderdeel3.D7
  N8: Matrix_keypad2.col2, Onderdeel3.D6_PWM
  N9: Matrix_keypad2.col3, Onderdeel3.D5_PWM
  N10: Matrix_keypad2.col4, Onderdeel3.D4
  N11: Matrix_keypad2.row1, Onderdeel3.D3_PWM
  N12: Matrix_keypad2.row2, Onderdeel3.D2
  N13: Matrix_keypad2.row3, Onderdeel3.D1/TX
  N14: Matrix_keypad2.row4, Onderdeel3.D0/RX

custom parts:
  KEYPAD 4x4: Matrix keypad 16 buttons, 4 rows x 4 columns
